# Fritzing sketch NumberMagic (saved by Fritzing 0.9.10b)
breadboards: 1

parts:
  Composant1 = Arduino Uno (Rev3)
  Keypad4x1 = Keypad Membran 4x4
  U2 = MAX7219 [package=dil24]
  LED1 = 5641AS-1 [part_number=5641AS-1 package="DIP (Dual Inline) [THT]"]
  R1 = Resistor [tolerance=±5% resistance=4.7k power=0.25 package=THT]
  R2 = Resistor [tolerance=±5% resistance=22k power=0.25 package=THT]
  C1 = Electrolytic Capacitor [capacitance=10µF voltage=50V package="100 mil [THT, electrolytic]"]
  C2 = Ceramic Capacitor [capacitance=100nF voltage=35V package="100 mil [THT, multilayer]"]
  LCD2 = LCD screen
  LCM1602_IIC2 = LCM1602 IIC [part_number="LCM1602 IIC" chip_label="LCM1602 IIC" package="DIP (Dual Inline) [THT]"]

nets:
  N1: Composant1.A1, U2.LOAD
  N2: Composant1.A4/SDA, LCM1602_IIC2.SDA
  N3: Composant1.A5/SCL, LCM1602_IIC2.SCL
  N4: Composant1.D8, Keypad4x1.Pin2
  N5: Composant1.D9_PWM, Keypad4x1.Pin1
  N6: Composant1.D11_PWM/MOSI, U2.DIN
  N7: Composant1.D13/SCK, U2.CLK
  N8: Composant1.D2, Keypad4x1.Pin8
  N9: Composant1.D3_PWM, Keypad4x1.Pin7
  N10: Composant1.D4, Keypad4x1.Pin6
  N11: Composant1.D5_PWM, Keypad4x1.Pin5
  N12: Composant1.D6_PWM, Keypad4x1.Pin4
  N13: Composant1.D7, Keypad4x1.Pin3
  VCC: Composant1.5V, U2.VCC, R2.Pin_0, C1.+, C2.1, LCM1602_IIC2.VCC
  GND: Composant1.GND, U2.GND, U2.GND2, C1.-, C2.0, LCM1602_IIC2.GND
  N14: U2.DIG0, LED1.cat1
  N15: U2.DIG2, LED1.cat3
  N16: U2.DIG3, LED1.cat4
  N17: U2.DIG1, LED1.cat2
  N18: U2.SEGA, LED1.anA
  N19: U2.SEGF, LED1.anF
  N20: U2.SEGB, LED1.anB
  N21: U2.SEGG, LED1.anG
  N22: U2.ISET, R1.Pin_1
  N23: U2.SEGC, LED1.anC
  N24: U2.SEGE, LED1.anE
  N25: U2.SEGDP, LED1.anDP
  N26: U2.SEGD, LED1.anD
  N27: R1.Pin_0, R2.Pin_1
  VSS: LCD2.VSS, LCM1602_IIC2.VSS
  VDD: LCD2.VDD, LCM1602_IIC2.VDD
  N28: LCD2.V0, LCM1602_IIC2.V0
  N29: LCD2.RS, LCM1602_IIC2.RS
  N30: LCD2.R/W, LCM1602_IIC2.RW
  N31: LCD2.E, LCM1602_IIC2.E
  N32: LCD2.DB0, LCM1602_IIC2.D0
  N33: LCD2.DB1, LCM1602_IIC2.D1
  N34: LCD2.DB2, LCM1602_IIC2.D2
  N35: LCD2.DB3, LCM1602_IIC2.D3
  N36: LCD2.DB4, LCM1602_IIC2.D4
  N37: LCD2.DB5, LCM1602_IIC2.D5
  N38: LCD2.DB6, LCM1602_IIC2.D6
  N39: LCD2.DB7, LCM1602_IIC2.D7
  N40: LCD2.LED+, LCM1602_IIC2.A
  N41: LCD2.LED-, LCM1602_IIC2.K
  N42: LCM1602_IIC2.LED_A, LCM1602_IIC2.LED_B

custom parts:
  Keypad Membran 4x4: Membrane Keypad 4x4 Matrix
  5641AS-1: 4 digit 7 segment common cathode LED display
  LCM1602 IIC: I2C-Module to use a 1602 or 2004 LCD on with the wire.h libory Serial LCD Modul
